# Fritzing sketch gateway (saved by Fritzing 0.9.5d)

parts:
  Raspberry_Pi_1 = Raspberry Pi 3 [part_number=RPI-3-V1.2]
  TTGO_LoRa_T3_1_6 = ESP32 TTGO LoRa T3_1.6

nets:
  N1: Raspberry_Pi_1.GPIO19, TTGO_LoRa_T3_1_6.14
  GND: Raspberry_Pi_1.GND, TTGO_LoRa_T3_1_6.23, TTGO_LoRa_T3_1_6.GND
  N2: Raspberry_Pi_1.GPIO18, TTGO_LoRa_T3_1_6.4

custom parts:
  ESP32 TTGO LoRa T3_1.6: LILYGO TTGO LoRa T3_1.6 Development Board. Protoboard Only.
