# Fritzing sketch node (saved by Fritzing 0.9.5d)

parts:
  TTGO_LoRa_T3_1_6 = ESP32 TTGO LoRa T3_1.6
  Tiny_RTC1 = Tiny RTC
  Arduino_Nano = Arduino Nano (Rev3.0)

nets:
  N1: TTGO_LoRa_T3_1_6.14, Tiny_RTC1.SCL, Arduino_Nano.D3
  N2: TTGO_LoRa_T3_1_6.4, Tiny_RTC1.SDA, Arduino_Nano.D2
  GND: TTGO_LoRa_T3_1_6.RST, Tiny_RTC1.GND, Arduino_Nano.GND

custom parts:
  ESP32 TTGO LoRa T3_1.6: LILYGO TTGO LoRa T3_1.6 Development Board. Protoboard Only.
  Tiny RTC: Tiny RTC I2C module DS1370Z RTC and AT24C32 EEPROM
